# Fritzing sketch drone (saved by Fritzing 0.9.3b)

parts:
  Part1 = Arduino 101
  NRF24L1 = NRF24L01
  GY1 = MPU-6050 Board GY-521 [form="♀ (female)" package=THT]
  920KV_Motor1 = DJI 920 KV Motor
  920KV_Motor2 = DJI 920 KV Motor
  920KV_Motor3 = DJI 920 KV Motor
  920KV_Motor4 = DJI 920 KV Motor
  BATT1 = LiPoly Battery (1300mAh)
  R3 = 220 Ω Resistor [package=THT]
  M6 = ESC
  M8 = ESC
  M7 = ESC
  M5 = ESC

nets (from the schematic view):
  N1: Part1.A4/SDA, GY1.pin4
  N2: Part1.A5/SCL, GY1.pin3
  N3: Part1.D8, NRF24L1.CSN
  N4: Part1.D9_PWM, M5.DATA
  N5: Part1.D11_PWM/MOSI, NRF24L1.MOSI
  N6: Part1.D12/MISO, NRF24L1.MISO
  N7: Part1.D13/SCK, NRF24L1.SCK
  GND: Part1.GND, M6.GND, M5.GND
  N8: Part1.D3_PWM, M7.DATA
  N9: Part1.D5_PWM, M8.DATA
  N10: Part1.D6_PWM, M6.DATA
  N11: Part1.D7, NRF24L1.CE
  3V3: Part1.3V3, NRF24L1.VCC, GY1.pin1
  GND_2: Part1.VIN, NRF24L1.GND, GY1.pin2, M8.GND, M7.GND
  N12: 920KV_Motor1.w, M5.W
  N13: 920KV_Motor1.v, M5.V
  N14: 920KV_Motor1.u, M5.U
  N15: 920KV_Motor2.w, M6.W
  N16: 920KV_Motor2.v, M6.V
  N17: 920KV_Motor2.u, M6.U
  N18: 920KV_Motor3.w, M7.W
  N19: 920KV_Motor3.v, M7.V
  N20: 920KV_Motor3.u, M7.U
  N21: 920KV_Motor4.w, M8.W
  N22: 920KV_Motor4.v, M8.V
  N23: 920KV_Motor4.u, M8.U
  N24: BATT1.positive, R3.input+
  N25: BATT1.negative, R3.Gnd
  GND2: R3.Gnd2, R3.Gnd3, R3.Gnd4, R3.Gnd5, M6.pin_13, M8.pin_13, M7.pin_13, M5.pin_13
  N26: R3.out1, R3.out2, R3.out3, R3.out4, M6.pin_14, M8.pin_14, M7.pin_14, M5.pin_14

custom parts:
  Arduino 101: A learning and development board that delivers the performance and low-power consumption of the Intel® Curie™ Module with the simplicity of Arduino at an entry-level price. It keeps the same robust form factor and peripheral list of the UNO with the addition of onboard Bluetooth LE capabilities and a 6-axis accelerometer/gyro to help you easily expand your creativity into the connected world.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
  NRF24L01: NRF24L01 module
  MPU-6050 Board GY-521: Acelerometro y Giroscopio MPU-6050 Board GY-521
  DJI 920 KV Motor: DJI Brushless Outrunner 2212/920K Motor F330-550
  LiPoly Battery (1300mAh): Lithium Ion Polymer Battery (1300mAh)
  220 Ω Resistor: A generic resistor (0.25W)
