# Fritzing sketch TRANSMITTER (saved by Fritzing 0.9.3b)

parts:
  Part1 = Thumb Joystick
  Part2 = Arduino Uno (Rev3)
  Part3 = Thumb Joystick
  NRF24L1 = NRF24L01

nets:
  GND: Part1.GND, Part2.GND, Part3.GND, NRF24L1.GND
  N1: Part1.HORZ, Part2.A3
  N2: Part1.VERT, Part2.A2
  VCC: Part1.VCC, Part2.5V, Part3.VCC
  N3: Part2.A0, Part3.VERT
  N4: Part2.A1, Part3.HORZ
  N5: Part2.D8, NRF24L1.CSN
  N6: Part2.D11_PWM/MOSI, NRF24L1.MOSI
  N7: Part2.D12/MISO, NRF24L1.MISO
  N8: Part2.D13/SCK, NRF24L1.SCK
  N9: Part2.D7, NRF24L1.CE
  3V3: Part2.3V3, NRF24L1.VCC

custom parts:
  NRF24L01: NRF24L01 module
